# Fritzing sketch Sleep_coach_tiny_schematic (saved by Fritzing 0.7.12b)
breadboards: 1

parts:
  C9 = Electrolytic Capacitor [capacitance=10µF package="100 mil [THT, electrolytic]"]
  Power_plug2 = Power plug
  LED1 = LED - 5mm [color="Blue (525nm)" package="5 mm [THT]"]
  LED2 = LED - 5mm [color="Blue (525nm)" package="5 mm [THT]"]
  LED4 = LED - 5mm [color="Blue (525nm)" package="5 mm [THT]"]
  S1 = Pushbutton [package="[THT]"]
  J1 = female pin header, 1 pin [form="♀ (female)"]
  J2 = female pin header, 1 pin [form="♀ (female)"]
  J3 = female pin header, 1 pin [form="♀ (female)"]
  R1 = Resistor [tolerance=±5% resistance=220 package=THT]
  R2 = Resistor [tolerance=±5% resistance=220 package=THT]
  R3 = Resistor [tolerance=±5% resistance=220 package=THT]
  R4 = Resistor [tolerance=±5% resistance=220 package=THT]
  U1 = attiny85 [package=dip]
  R6 = Resistor [tolerance=±5% resistance=220 package=THT]
  LED3 = LED - 5mm [color="Blue (525nm)" package="5 mm [THT]"]

nets:
  N1: C9.-, Power_plug2.GND, J1.pin1, R1.Pin_0, R2.Pin_0, R3.Pin_1, R4.Pin_1, U1.Pin_4, R6.Pin_0
  N2: C9.+, Power_plug2.VCC, S1.Pin_3, S1.Pin_4, J2.pin1, U1.Pin_8
  N3: LED1.cathode, R1.Pin_1
  N4: LED1.anode, LED2.anode, LED4.anode, U1.Pin_5, LED3.anode
  N5: LED2.cathode, R3.Pin_0
  N6: LED4.cathode, R4.Pin_0
  N7: S1.Pin_1, S1.Pin_2, U1.Pin_6, R6.Pin_1
  N8: J3.pin1, U1.Pin_2
  N9: R2.Pin_1, LED3.cathode
